# Fritzing sketch esp32-circuit (saved by Fritzing 0.9.10b)
perfboards: 1

parts:
  LED1 = LED - 3mm [color="Red (633nm)" current=0.030 package="3 mm [THT]"]
  R1 = Resistor [tolerance=±5% resistance=220 package="0603 [SMD]"]
  F1 = Fan - 4 wire [package=THT]
  R2 = Rotary Potentiometer (Small) [maximum_resistance=100kΩ knob_status=50% power=0.5W package=THT]
  U1 = ESP32-38PinWide [part_number=ESP32-38PinWide]
  U2 = Mini-360 DC-DC Buck converter [package=THT]
  JP1 = Header 2 [package=r_sw_th]
  J1 = Power Jack [package=power_jack_smd]

nets:
  N1: LED1.cathode, R2.leg2, U1.GND
  N2: LED1.anode, R1.Pin_1
  N3: R1.Pin_0, U1.GPIO18
  N4: F1.GND, U2.IN-, J1.GNDBREAK
  N5: F1.Power, U2.IN+, JP1.1
  N6: F1.Tach, U1.GPIO33
  N7: R2.leg1, U1.3.3
  N8: R2.wiper, U1.GPIO32
  N9: U1.GPIO11, U2.OUT-
  N10: U1.VIN, U2.OUT+
  N11: JP1.2, J1.PWR

custom parts:
  Fan - 4 wire: Fan, 4 wire with tach.
  ESP32-38PinWide: Generic 38-Pin ESP32 with wide format (only access to one side of pins on a breadboard) based on Stephen Lilley's HiLetgo ESP-WROOM-32 ESP32 ESP-32S Development Board.
  Mini-360 DC-DC Buck converter: Mini-360 DC-DC Buck converter. Tiny buck step down voltage converter, input voltage 4.75 to 23V output 1 to 17V adjustable. Available from ebay and the like.
